# Fritzing sketch AMSE_Presentation_Wiring_Diagram (saved by Fritzing 0.9.4)

parts:
  920KV_Motor1 = DJI 920 KV Motor
  M1 = ESC
  Part1 = Arduino Mega 2560 (Rev3)
  BAT1 = 12v battery [package=battery]  # not connected

nets:
  N1: 920KV_Motor1.w, M1.W
  N2: 920KV_Motor1.v, M1.V
  N3: 920KV_Motor1.u, M1.U
  N4: M1.DATA, Part1.D37
  GND: M1.GND, Part1.GND
  5V: M1.5V, Part1.5V

notes:
  ADAPTER

custom parts:
  DJI 920 KV Motor: DJI Brushless Outrunner 2212/920K Motor F330-550
  12v battery: 12V lead acid battery 12ah
